# Fritzing sketch Color Sensor (saved by Fritzing 0.9.3b)

parts:
  Part1 = Arduino Nano (Rev3.0)
  Part2 = adafruit [part_number="Adafruit #1334"]

nets:
  N1: Part1.D2, Part2.connector12
  N2: Part1.D3, Part2.connector11
  N3: Part1.GND, Part2.connector9
  N4: Part1.5V, Part2.connector10
