# Fritzing sketch Neo Pixel (saved by Fritzing 0.9.3b)

parts:
  Part1 = Arduino Nano (Rev3.0)
  LED1 = prefix0000

nets:
  N1: Part1.D6, LED1.connector2
  N2: Part1.GND, LED1.connector3
  N3: Part1.5V, LED1.connector1
