# Fritzing sketch final board (saved by Fritzing 0.9.3b)

parts:
  Part3 = Arduino Nano (Rev3.0)
  Part4 = Adafruit TCS34725 RGB Color Sensor [part_number="Adafruit #1334"]
  LED1 = prefix0000
  Part5 = Adafruit VS1053 Codec + MicroSD Breakout - MP3/WAV/MIDI/OGG [part_number="Adafruit #1381"]
  TRS1 = Audio Jack (TRS) 3.5mm [package="4Ucon 08780 [THT]"]

nets:
  N1: Part3.D2, Part4.SDA
  N2: Part3.D3, Part4.SCL
  N3: Part3.D6, LED1.connector2
  N4: Part3.D9, Part5.RST_5V
  N5: Part3.D10, Part5.RX_5V
  GND: Part3.GND, Part4.GND, LED1.connector3, Part5.GND, Part5.GPIO0
  5V: Part3.5V, Part4.+3V3, LED1.connector1
  3V3: Part3.3V3, Part5.3.3V, Part5.GPIO1
  N6: Part5.R_OUT, TRS1.Ring
  N7: Part5.L_OUT, TRS1.Tip
  N8: Part5.AGND, TRS1.Sleeve

custom parts:
  Adafruit TCS34725 RGB Color Sensor: Your electronics can now see in dazzling color with this lovely color light sensor. We found the best color sensor on the market, the TCS34725, which has RGB and Clear light sensing elements. An IR blocking filter, integrated on-chip and localized to the color sensing photodiodes, minimizes the IR spectral component of the incoming light and allows color measurements to be made accurately. The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
  Adafruit VS1053 Codec + MicroSD Breakout - MP3/WAV/MIDI/OGG: This breakout board is the ultimate companion for the VLSI VS1053B DSP codec chip. The VS1053 can decode a wide variety of audio formats such as MP3, AAC, Ogg Vorbis, WMA, MIDI, FLAC, WAV (PCM and ADPCM). It can also be used to record audio in both PCM (WAV) and compressed Ogg Vorbis. You can do all sorts of stuff with the audio as well such as adjusting bass, treble, and volume digitally.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
