# Fritzing sketch iLuminator (saved by Fritzing 0.9.3b)

parts:
  Part1 = Arduino Micro (Rev3)
  Part2 = FemtoBuck LED Driver
  Part3 = FemtoBuck LED Driver
  Part4 = FemtoBuck LED Driver

nets:
  N1: Part1.GND, Part2.D-
  N2: Part1.A2, Part4.D+
  N3: Part1.A1, Part3.D+
  N4: Part1.A0, Part2.D+

notes:
  LED Strips
  DC power 12V mx
  Connect as many LED Drivers you want
